// Logisim project PIC_8_IOs.circ as structural Verilog: 20 circuits, main circuit Interrupt_Request_Register
module main (
  input  [7:0] in_1
);

  wire ADD_Match_0, button_1_out, button_2_out, button_3_out, button_4_out, button_5_out, button_6_out,
       button_7_out, button_8_out, button_9_out, button_10_out, button_11_out, button_12_out, button_13_out,
       clock_1_out, clock_2_out, clock_3_out, clock_4_out, clock_5_out, clock_6_out, clock_7_out,
       clock_8_out, clock_9_out, cpu_1_cpu_busy, INT, INT_0, INT_1, INT_2, INT_3, INT_4, INT_5, INT_6, INT_7,
       INT_A, IRR_RAM_En, priority_arbiter_1_custom_mode, priority_arbiter_1_default_mode,
       program_controller_1_chrr_bus_en, program_controller_1_imr_bus_en, program_controller_1_irr_bus_en,
       program_controller_1_pa_bus_en, program_controller_1_reset, RAM_En, READ, Reset_CNT, Reset_RAM_0,
       Reset_ROM_1, rgbled_1_p1, rgbled_1_p2, ROM_En, RST_IRR_CNT, RST_PA_CNT, WRITE;
  wire [2:0] counter_6_q;
  wire [3:0] counter_4_q;
  wire [4:0] counter_1_q, counter_2_q, counter_3_q, counter_5_q;
  wire [7:0] cpu_1_address, I_O_0_data_out, interrupt_mask_register_1_mask_out,
       interrupt_request_register_1_ir_out_arbiter, interrupt_request_register_1_ir_out_bus, IRR_RAM_Out,
       PA_List_In, priority_arbiter_1_chr_out, priority_arbiter_1_next_priority, ram_1_data, READ_IO,
       rom_1_data, WRITE_IO;

  Counter #(.width(5), .max('h1f)) counter_1 (
    .clr(Reset_RAM_0), .count(ADD_Match_0), .clk(clock_1_out), .Q(counter_1_q));  // open: load, up, D, carry
  Clock clock_1 (.out(clock_1_out));
  Counter #(.width(5), .max('h1f)) counter_2 (
    .clr(Reset_ROM_1), .clk(clock_2_out), .Q(counter_2_q));  // open: load, up, count, D, carry
  Clock clock_2 (.out(clock_2_out));
  // Probe on interrupt_mask_register_1_mask_out
  Interrupt_Mask_Register interrupt_mask_register_1 (
    .MASK_Out(interrupt_mask_register_1_mask_out), .MASK_In_BUS(interrupt_request_register_1_ir_out_bus),
    .BUS_En(program_controller_1_imr_bus_en));
  RAM #(.addrWidth(5)) ram_1 (.addr(counter_1_q), .we(ADD_Match_0), .oe(1'b0), .clk(clock_3_out), .data(ram_1_data));
  Clock clock_3 (.out(clock_3_out));
  ROM #(.addrWidth(5)) rom_1 (.addr(counter_2_q), .data(rom_1_data));
  // Probe on interrupt_request_register_1_ir_out_arbiter
  Interrupt_Request_Register interrupt_request_register_1 (
    .IR_2(INT_2), .IR_5(INT_5), .IR_0(INT_0), .IR_6(INT_6), .IR_7(INT_7), .IR_4(INT_4),
    .Mask(interrupt_mask_register_1_mask_out), .IR_3(INT_3), .IR_1(INT_1),
    .IR_Out_Arbiter(interrupt_request_register_1_ir_out_arbiter),
    .IR_Out_BUS(interrupt_request_register_1_ir_out_bus), .BUS_En(program_controller_1_irr_bus_en));
  // Probe on priority_arbiter_1_next_priority
  LED led_1 (.in(INT));
  Priority_Arbiter priority_arbiter_1 (
    .CHR_OUT(priority_arbiter_1_chr_out), .INT_Req(interrupt_request_register_1_ir_out_arbiter),
    .INT_A(INT_A), .PA_Bus_EN(program_controller_1_pa_bus_en),
    .BUS_Input(interrupt_request_register_1_ir_out_bus), .INT(INT),
    .Next_Priority(priority_arbiter_1_next_priority), .Default_Mode(priority_arbiter_1_default_mode),
    .Custom_Mode(priority_arbiter_1_custom_mode));
  // Probe on interrupt_request_register_1_ir_out_bus
  LED led_2 (.in(INT_A));
  LED led_3 (.in(priority_arbiter_1_default_mode));
  LED led_4 (.in(priority_arbiter_1_custom_mode));
  Button button_1 (.out(button_1_out));
  Button button_2 (.out(button_2_out));
  Button button_3 (.out(button_3_out));
  Button button_4 (.out(button_4_out));
  Button button_5 (.out(button_5_out));
  Button button_6 (.out(button_6_out));
  Button button_7 (.out(button_7_out));
  Button button_8 (.out(button_8_out));
  // Probe on priority_arbiter_1_chr_out
  LED led_5 (.in(INT_0));
  I_O I_O_0 (
    .ADD_Match(ADD_Match_0), .RE_WR(1'b1), .RAM_Out(ram_1_data), .INT_In(button_1_out), .INT(INT_0),
    .DATA_In(I_O_0_data_out), .Address_In(8'ha0), .Address(cpu_1_address), .DATA_Out(I_O_0_data_out),
    .Reset_RAM(Reset_RAM_0));  // open: ROM_In, Reset_ROM
  LED led_6 (.in(INT_1));
  I_O I_O_1 (
    .RE_WR(1'b0), .INT_In(button_2_out), .INT(INT_1), .DATA_In(I_O_0_data_out), .ROM_In(rom_1_data),
    .Address_In(8'ha1), .Address(cpu_1_address), .DATA_Out(I_O_0_data_out), .Reset_ROM(Reset_ROM_1));  // open: ADD_Match, RAM_Out, Reset_RAM
  LED led_7 (.in(INT_2));
  I_O I_O_2 (
    .RE_WR(1'b1), .INT_In(button_3_out), .INT(INT_2), .DATA_In(I_O_0_data_out), .Address_In(8'ha2),
    .Address(cpu_1_address), .DATA_Out(I_O_0_data_out));  // open: ADD_Match, RAM_Out, ROM_In, Reset_RAM, Reset_ROM
  LED led_8 (.in(INT_3));
  I_O I_O_3 (
    .RE_WR(1'b1), .INT_In(button_4_out), .INT(INT_3), .DATA_In(I_O_0_data_out), .Address_In(8'ha3),
    .Address(cpu_1_address), .DATA_Out(I_O_0_data_out));  // open: ADD_Match, RAM_Out, ROM_In, Reset_RAM, Reset_ROM
  LED led_9 (.in(INT_4));
  I_O I_O_4 (
    .RE_WR(1'b1), .INT_In(button_5_out), .INT(INT_4), .DATA_In(I_O_0_data_out), .Address_In(8'ha4),
    .Address(cpu_1_address), .DATA_Out(I_O_0_data_out));  // open: ADD_Match, RAM_Out, ROM_In, Reset_RAM, Reset_ROM
  LED led_10 (.in(INT_5));
  I_O I_O_5 (
    .RE_WR(1'b1), .INT_In(button_6_out), .INT(INT_5), .DATA_In(I_O_0_data_out), .Address_In(8'ha5),
    .Address(cpu_1_address), .DATA_Out(I_O_0_data_out));  // open: ADD_Match, RAM_Out, ROM_In, Reset_RAM, Reset_ROM
  LED led_11 (.in(INT_6));
  I_O I_O_6 (
    .RE_WR(1'b1), .INT_In(button_7_out), .INT(INT_6), .DATA_In(I_O_0_data_out), .Address_In(8'ha6),
    .Address(cpu_1_address), .DATA_Out(I_O_0_data_out));  // open: ADD_Match, RAM_Out, ROM_In, Reset_RAM, Reset_ROM
  LED led_12 (.in(INT_7));
  I_O I_O_7 (
    .RE_WR(1'b1), .INT_In(button_8_out), .INT(INT_7), .DATA_In(I_O_0_data_out), .Address_In(8'ha7),
    .Address(cpu_1_address), .DATA_Out(I_O_0_data_out));  // open: ADD_Match, RAM_Out, ROM_In, Reset_RAM, Reset_ROM
  // Probe on I_O_0_data_out
  Currently_Handled_Request_Register currently_handled_request_register_1 (
    .CHR_Out_BUS(interrupt_request_register_1_ir_out_bus), .CHR_In(priority_arbiter_1_chr_out),
    .BUS_En(program_controller_1_chrr_bus_en), .Reset(program_controller_1_reset));
  // Probe on cpu_1_address
  // RGBLED rgbled_1: pin names not known; wires that end beside it: rgbled_1_p1, rgbled_1_p2
  LED led_13 (.in(INT_A));
  Program_Controller program_controller_1 (
    .IMR_BUS_En(program_controller_1_imr_bus_en), .IRR_BUS_En(program_controller_1_irr_bus_en),
    .CHRR_BUS_En(program_controller_1_chrr_bus_en), .PA_BUS_En(program_controller_1_pa_bus_en),
    .WRITE(WRITE), .READ(READ), .DATA_In(I_O_0_data_out), .INT_A(INT_A),
    .PC_In_BUS(interrupt_request_register_1_ir_out_bus),
    .PC_Out_BUS(interrupt_request_register_1_ir_out_bus), .DATA_Out(I_O_0_data_out),
    .Reset(program_controller_1_reset));
  LED led_14 (.in(cpu_1_cpu_busy));
  Button button_9 (.out(button_9_out));
  Button button_10 (.out(button_10_out));
  Button button_11 (.out(button_11_out));
  Button button_12 (.out(button_12_out));
  Button button_13 (.out(button_13_out));
  Counter #(.width(5), .max('h1f)) counter_3 (
    .clr(Reset_CNT), .count(ROM_En), .clk(clock_4_out), .Q(counter_3_q));  // open: load, up, D, carry
  Clock clock_4 (.out(clock_4_out));
  ROM #(.addrWidth(5)) rom_2 (.addr(counter_3_q), .data(READ_IO));
  Clock clock_5 (.out(clock_5_out));
  RAM #(.addrWidth(4), .databus("bibus")) ram_2 (
    .addr(counter_4_q), .we(IRR_RAM_En), .oe(1'b0), .clk(clock_6_out), .din(IRR_RAM_Out));  // open: dout
  Clock clock_6 (.out(clock_6_out));
  LED led_15 (.in(INT_A));
  LED led_16 (.in(INT));
  Counter #(.width(4), .max('hf)) counter_4 (
    .clr(RST_IRR_CNT), .count(IRR_RAM_En), .clk(clock_5_out), .Q(counter_4_q));  // open: load, up, D, carry
  CPU cpu_1 (
    .ROM_En(ROM_En), .Address(cpu_1_address), .read_IRR(button_13_out), .INT(INT), .DATA_In(I_O_0_data_out),
    .set_PA_default(button_10_out), .PA_List_In(PA_List_In), .CPU_Busy(cpu_1_cpu_busy), .READ_IO(READ_IO),
    .Reset_CNT(Reset_CNT), .write_MASK(button_12_out), .READ(READ), .WRITE_IO(WRITE_IO),
    .DATA_Out(I_O_0_data_out), .WRITE(WRITE), .write_to_PA(button_11_out), .MASK_In(in_1),
    .INT_A_In(button_9_out), .INT_A(INT_A), .RAM_En(RAM_En), .PA_ERROR(rgbled_1_p1),
    .PA_success(rgbled_1_p2), .Reset_PA_CNT(RST_PA_CNT), .Reset_IRR_CTR(RST_IRR_CNT),
    .IRR_RAM_En(IRR_RAM_En), .IRR_RAM_Out(IRR_RAM_Out));
  Clock clock_7 (.out(clock_7_out));
  RAM #(.addrWidth(5), .databus("bibus")) ram_3 (
    .addr(counter_5_q), .we(RAM_En), .oe(1'b0), .clk(clock_8_out), .din(WRITE_IO));  // open: dout
  Clock clock_8 (.out(clock_8_out));
  Counter #(.width(5), .max('h1f)) counter_5 (
    .clr(Reset_CNT), .count(RAM_En), .clk(clock_7_out), .Q(counter_5_q));  // open: load, up, D, carry
  ROM #(.addrWidth(3)) rom_3 (.addr(counter_6_q), .data(PA_List_In));
  Counter #(.width(3), .max('h7)) counter_6 (
    .clr(RST_PA_CNT), .clk(clock_9_out), .Q(counter_6_q));  // open: load, up, count, D, carry
  Clock clock_9 (.out(clock_9_out));

  // Notes on the sheet:
  //   contents of rom_1 (hex, n*v repeats v):
  //   54 1 38 67 28 46 89 55 fb a8 c6 22 77 aa 55 aa 55
  //   Internal BUS
  //   contents of rom_2 (hex, n*v repeats v):
  //   54 1 38 67 28 46 89 55 fb a8 c6 22 77 aa 55 aa 55
  //   DATA_to_IO
  //   DATA_from_IRR
  //   contents of rom_3 (hex, n*v repeats v):
  //   2 2 1 8 10 20 40 80
  //   DATA_from_IO
  //   LIST_to_PA
endmodule

module Interrupt_Request_Register (
  input  IR_0,
  input  IR_1,
  input  IR_2,
  input  IR_3,
  input  BUS_En,
  input  IR_4,
  input  IR_5,
  input  IR_6,
  input  IR_7,
  input  [7:0] Mask,
  output [7:0] IR_Out_Arbiter,
  output [7:0] IR_Out_BUS
);

  wire not_1_out, not_2_out, not_3_out, not_4_out, not_5_out, not_6_out, not_7_out, not_8_out;

  assign IR_Out_Arbiter[0] = Mask[0] ? IR_0 : 1'bz;  // Controlled_Buffer controlled_buffer_1
  not not_1 (not_1_out, Mask[0]);
  assign IR_Out_Arbiter[0] = not_1_out ? 1'b0 : 1'bz;  // Controlled_Buffer controlled_buffer_2
  assign IR_Out_Arbiter[1] = Mask[1] ? IR_1 : 1'bz;  // Controlled_Buffer controlled_buffer_3
  not not_2 (not_2_out, Mask[1]);
  assign IR_Out_Arbiter[1] = not_2_out ? 1'b0 : 1'bz;  // Controlled_Buffer controlled_buffer_4
  assign IR_Out_Arbiter[2] = Mask[2] ? IR_2 : 1'bz;  // Controlled_Buffer controlled_buffer_5
  not not_3 (not_3_out, Mask[2]);
  assign IR_Out_Arbiter[2] = not_3_out ? 1'b0 : 1'bz;  // Controlled_Buffer controlled_buffer_6
  assign IR_Out_Arbiter[3] = Mask[3] ? IR_3 : 1'bz;  // Controlled_Buffer controlled_buffer_7
  not not_4 (not_4_out, Mask[3]);
  assign IR_Out_Arbiter[3] = not_4_out ? 1'b0 : 1'bz;  // Controlled_Buffer controlled_buffer_8
  assign IR_Out_Arbiter[4] = Mask[4] ? IR_4 : 1'bz;  // Controlled_Buffer controlled_buffer_9
  not not_5 (not_5_out, Mask[4]);
  assign IR_Out_Arbiter[4] = not_5_out ? 1'b0 : 1'bz;  // Controlled_Buffer controlled_buffer_10
  assign IR_Out_Arbiter[5] = Mask[5] ? IR_5 : 1'bz;  // Controlled_Buffer controlled_buffer_11
  not not_6 (not_6_out, Mask[5]);
  assign IR_Out_Arbiter[5] = not_6_out ? 1'b0 : 1'bz;  // Controlled_Buffer controlled_buffer_12
  assign IR_Out_Arbiter[6] = Mask[6] ? IR_6 : 1'bz;  // Controlled_Buffer controlled_buffer_13
  not not_7 (not_7_out, Mask[6]);
  assign IR_Out_Arbiter[6] = not_7_out ? 1'b0 : 1'bz;  // Controlled_Buffer controlled_buffer_14
  assign IR_Out_Arbiter[7] = Mask[7] ? IR_7 : 1'bz;  // Controlled_Buffer controlled_buffer_15
  not not_8 (not_8_out, Mask[7]);
  assign IR_Out_Arbiter[7] = not_8_out ? 1'b0 : 1'bz;  // Controlled_Buffer controlled_buffer_16
  assign IR_Out_BUS = BUS_En ? IR_Out_Arbiter : 8'bz;  // Controlled_Buffer controlled_buffer_17
endmodule

module Interrupt_Mask_Register (
  input  [7:0] MASK_In_BUS,
  input  BUS_En,
  output [7:0] MASK_Out
);

  wire clock_1_out, not_2_out;
  wire [7:0] and_1_out, controlled_buffer_1_out, not_1_out, or_1_out;

  assign and_1_out = MASK_Out & not_1_out;  // AND_Gate and_1, 8 bits wide
  assign not_1_out = ~{8{BUS_En}};  // NOT_Gate not_1, 8 bits wide
  assign controlled_buffer_1_out = BUS_En ? MASK_In_BUS : 8'bz;  // Controlled_Buffer controlled_buffer_1
  assign controlled_buffer_1_out = not_2_out ? {8{1'b0}} : 8'bz;  // Controlled_Buffer controlled_buffer_2
  not not_2 (not_2_out, BUS_En);
  assign or_1_out = and_1_out | controlled_buffer_1_out;  // OR_Gate or_1, 8 bits wide
  Clock clock_1 (.out(clock_1_out));
  Register register_1 (.D(or_1_out), .en(1'b1), .clk(clock_1_out), .Q(MASK_Out));  // open: clr
endmodule

module Priority_Arbiter (
  input  [7:0] BUS_Input,
  input  PA_Bus_EN,
  input  INT_A,
  input  [7:0] INT_Req,
  output [7:0] Next_Priority,
  output Custom_Mode,
  output [7:0] CHR_OUT,
  output Default_Mode,
  output INT
);

  wire clock_1_out, clock_2_out, interrupt_request_priority_examinator_1_int_a_out,
       interrupt_request_priority_examinator_1_new_req, interrupt_request_priority_examinator_1_req_found,
       interrupt_request_priority_examinator_1_reset, list_mode_controller_1_writing_counter_reset,
       list_mode_controller_1_writing_enable;
  wire [2:0] address_counter_1_address, controlled_buffer_1_out, controlled_buffer_3_out, register_1_q,
       writing_counter_1_address;
  wire [7:0] Default_Priority_List_data, Programmable_Priority_List_data;

  Writing_Counter writing_counter_1 (
    .Address(writing_counter_1_address), .Reset(list_mode_controller_1_writing_counter_reset));
  assign controlled_buffer_1_out = PA_Bus_EN ? writing_counter_1_address : 3'bz;  // Controlled_Buffer controlled_buffer_1
  assign controlled_buffer_1_out = Custom_Mode ? address_counter_1_address : 3'bz;  // Controlled_Buffer controlled_buffer_2
  assign controlled_buffer_3_out = Default_Mode ? address_counter_1_address : 3'bz;  // Controlled_Buffer controlled_buffer_3
  Address_Counter address_counter_1 (
    .Address(address_counter_1_address), .Found(interrupt_request_priority_examinator_1_req_found),
    .Reset(interrupt_request_priority_examinator_1_reset));
  Clock clock_1 (.out(clock_1_out));
  Register #(.width(3)) register_1 (
    .D(controlled_buffer_3_out), .en(1'b1), .clk(clock_2_out), .Q(register_1_q));  // open: clr
  Clock clock_2 (.out(clock_2_out));
  RAM #(.addrWidth(3)) Programmable_Priority_List (
    .addr(controlled_buffer_1_out), .we(list_mode_controller_1_writing_enable), .oe(Custom_Mode),
    .clk(clock_1_out), .data(Programmable_Priority_List_data));
  ROM #(.addrWidth(3)) Default_Priority_List (.addr(register_1_q), .data(Default_Priority_List_data));
  List_Mode_Controller list_mode_controller_1 (
    .Default_Mode_Enabled(Default_Mode),
    .Writing_Counter_Reset(list_mode_controller_1_writing_counter_reset),
    .BUS_INPUT(Programmable_Priority_List_data), .PA_Bus_En(PA_Bus_EN), .Custom_Mode_Enabled(Custom_Mode),
    .Writing_Enable(list_mode_controller_1_writing_enable));
  assign Next_Priority = Default_Mode ? Default_Priority_List_data : 8'bz;  // Controlled_Buffer controlled_buffer_4
  assign Programmable_Priority_List_data = PA_Bus_EN ? BUS_Input : 8'bz;  // Controlled_Buffer controlled_buffer_5
  assign Next_Priority = Custom_Mode ? Programmable_Priority_List_data : 8'bz;  // Controlled_Buffer controlled_buffer_6
  Interrupt_Request_Priority_Examinator interrupt_request_priority_examinator_1 (
    .Req_Found(interrupt_request_priority_examinator_1_req_found), .PA_Bus_EN(PA_Bus_EN), .INT_A(INT_A),
    .CHR_OUT(CHR_OUT), .Reset(interrupt_request_priority_examinator_1_reset), .Next_Prio(Next_Priority),
    .INT_Req(INT_Req), .INT_A_OUT(interrupt_request_priority_examinator_1_int_a_out),
    .New_Req(interrupt_request_priority_examinator_1_new_req));
  Interrupt_Sender interrupt_sender_1 (
    .INT(INT), .Req_Found(interrupt_request_priority_examinator_1_req_found),
    .INT_A(interrupt_request_priority_examinator_1_int_a_out),
    .New_Req(interrupt_request_priority_examinator_1_new_req));

  // Notes on the sheet:
  //   contents of Default_Priority_List (hex, n*v repeats v):
  //   1 2 4 8 10 20 40 80
endmodule

module Interrupt_Request_Priority_Examinator (
  input  [7:0] INT_Req,
  input  PA_Bus_EN,
  input  [7:0] Next_Prio,
  input  INT_A,
  output New_Req,
  output Req_Found,
  output Reset,
  output [7:0] CHR_OUT,
  output INT_A_OUT
);

  wire and_2_out, and_3_out, clock_1_out, clock_2_out, clock_3_out, clock_4_out, d_ff_1_q, d_ff_1_qn,
       d_ff_2_q, d_ff_2_qn, nor_1_out, not_1_out, not_2_out, or_3_out, xor_1_out;
  wire [7:0] and_4_out, and_6_out, controlled_buffer_1_out, not_3_out, register_1_q;
  wire [7:7] and_1_out;

  not not_1 (not_1_out, INT_A);
  assign controlled_buffer_1_out = PA_Bus_EN ? {8{1'b0}} : 8'bz;  // Controlled_Buffer controlled_buffer_1
  not not_2 (not_2_out, PA_Bus_EN);
  assign controlled_buffer_1_out = not_2_out ? Next_Prio : 8'bz;  // Controlled_Buffer controlled_buffer_2
  and and_1 (and_1_out[7], d_ff_2_q, INT_A, d_ff_1_qn);
  and and_2 (and_2_out, d_ff_1_qn, not_1_out, d_ff_2_qn);
  Clock clock_1 (.out(clock_1_out));
  xor xor_1 (xor_1_out, d_ff_2_q, d_ff_1_q);
  and and_3 (and_3_out, xor_1_out, not_1_out);
  Clock clock_2 (.out(clock_2_out));
  Register register_1 (.D(INT_Req), .en(1'b1), .clk(clock_3_out), .Q(register_1_q));  // open: clr
  Clock clock_3 (.out(clock_3_out));
  nor nor_1 (nor_1_out, INT_Req[0], INT_Req[1], INT_Req[2], INT_Req[3], INT_Req[4], INT_Req[5], INT_Req[6], INT_Req[7]);
  assign and_4_out = INT_Req & controlled_buffer_1_out;  // AND_Gate and_4, 8 bits wide
  D_Flip_Flop d_ff_1 (.D(and_2_out), .clk(clock_1_out), .Q(d_ff_1_q), .Qn(d_ff_1_qn));  // open: preset, reset
  D_Flip_Flop d_ff_2 (.D(and_3_out), .clk(clock_2_out), .Q(d_ff_2_q), .Qn(d_ff_2_qn));  // open: preset, reset
  assign not_3_out = ~register_1_q;  // NOT_Gate not_3, 8 bits wide
  assign CHR_OUT = controlled_buffer_1_out & {8{and_1_out[7]}};  // AND_Gate and_5, 8 bits wide
  assign and_6_out = INT_Req & not_3_out;  // AND_Gate and_6, 8 bits wide
  or or_1 (Req_Found, and_4_out[0], and_4_out[1], and_4_out[2], and_4_out[3], and_4_out[4], and_4_out[5], and_4_out[6], and_4_out[7]);
  or or_2 (New_Req, and_6_out[0], and_6_out[1], and_6_out[2], and_6_out[3], and_6_out[4], and_6_out[5], and_6_out[6], and_6_out[7]);
  or or_3 (or_3_out, New_Req, nor_1_out, PA_Bus_EN, INT_A);
  D_Flip_Flop d_ff_3 (.D(or_3_out), .clk(clock_4_out), .Q(Reset));  // open: Qn, preset, reset
  Clock clock_4 (.out(clock_4_out));

  assign INT_A_OUT = INT_A;

  // Notes on the sheet:
  //   No requests
endmodule

module Interrupt_Sender (
  input  Req_Found,
  input  INT_A,
  input  New_Req,
  output INT
);

  wire and_1_out, and_2_out, and_3_out, and_4_out, and_5_out, and_6_out, and_7_out, and_8_out, and_9_out,
       clock_1_out, clock_2_out, clock_3_out, d_ff_1_q, d_ff_1_qn, d_ff_2_q, d_ff_2_qn, d_ff_3_q, d_ff_3_qn,
       nor_1_out, not_1_out, not_2_out, or_1_out, or_2_out, xor_1_out;

  not not_1 (not_1_out, INT_A);
  and and_1 (and_1_out, Req_Found, not_1_out, not_2_out);
  not not_2 (not_2_out, New_Req);
  and and_2 (and_2_out, d_ff_1_qn, d_ff_2_q, d_ff_3_qn);
  and and_3 (and_3_out, New_Req, d_ff_2_qn, d_ff_3_q);
  and and_4 (and_4_out, New_Req, d_ff_1_qn, d_ff_2_qn);
  and and_5 (and_5_out, INT_A, d_ff_1_qn, d_ff_3_qn);
  xor xor_1 (xor_1_out, d_ff_1_q, d_ff_2_q);
  and and_6 (and_6_out, d_ff_1_q, d_ff_2_q, d_ff_3_qn);
  and and_7 (and_7_out, New_Req, d_ff_2_qn, d_ff_3_q);
  and and_8 (and_8_out, New_Req, d_ff_1_qn, d_ff_2_qn);
  D_Flip_Flop d_ff_1 (.D(or_1_out), .clk(clock_1_out), .Q(d_ff_1_q), .Qn(d_ff_1_qn));  // open: preset, reset
  or or_1 (or_1_out, and_2_out, and_3_out, and_4_out, and_5_out);
  Clock clock_1 (.out(clock_1_out));
  D_Flip_Flop d_ff_2 (.D(and_9_out), .clk(clock_2_out), .Q(d_ff_2_q), .Qn(d_ff_2_qn));  // open: preset, reset
  and and_9 (and_9_out, d_ff_3_qn, xor_1_out);
  Clock clock_2 (.out(clock_2_out));
  D_Flip_Flop d_ff_3 (.D(or_2_out), .clk(clock_3_out), .Q(d_ff_3_q), .Qn(d_ff_3_qn));  // open: preset, reset
  or or_2 (or_2_out, and_6_out, and_7_out, and_8_out);
  Clock clock_3 (.out(clock_3_out));
  nor nor_1 (nor_1_out, INT_A, New_Req, d_ff_1_q, d_ff_2_q, d_ff_3_q);
  and and_10 (INT, and_1_out, nor_1_out);
endmodule

module List_Mode_Controller (
  input  [7:0] BUS_INPUT,
  input  PA_Bus_En,
  output Writing_Counter_Reset,
  output Custom_Mode_Enabled,
  output Default_Mode_Enabled,
  output Writing_Enable
);

  wire and_1_out, and_3_out, clock_1_out, clock_2_out, d_ff_1_qn, j_k_ff_1_qn, not_1_out, not_2_out,
       not_3_out, not_4_out, not_5_out, not_6_out, not_7_out, not_8_out;
  wire [7:0] controlled_buffer_1_out;

  D_Flip_Flop d_ff_1 (.D(PA_Bus_En), .clk(clock_1_out), .Qn(d_ff_1_qn));  // open: Q, preset, reset
  Clock clock_1 (.out(clock_1_out));
  and and_1 (and_1_out, PA_Bus_En, d_ff_1_qn);
  assign controlled_buffer_1_out = and_1_out ? BUS_INPUT : 8'bz;  // Controlled_Buffer controlled_buffer_1
  not not_1 (not_1_out, and_1_out);
  assign controlled_buffer_1_out = not_1_out ? {8{1'b0}} : 8'bz;  // Controlled_Buffer controlled_buffer_2
  not not_2 (not_2_out, controlled_buffer_1_out[0]);
  not not_3 (not_3_out, controlled_buffer_1_out[2]);
  not not_4 (not_4_out, controlled_buffer_1_out[4]);
  not not_5 (not_5_out, controlled_buffer_1_out[6]);
  not not_6 (not_6_out, controlled_buffer_1_out[0]);
  not not_7 (not_7_out, controlled_buffer_1_out[5]);
  and and_2 (Writing_Counter_Reset, not_2_out, controlled_buffer_1_out[1], not_3_out, controlled_buffer_1_out[3], not_4_out, controlled_buffer_1_out[5], not_5_out, controlled_buffer_1_out[7]);
  and and_3 (and_3_out, not_6_out, controlled_buffer_1_out[1], controlled_buffer_1_out[2], controlled_buffer_1_out[3], controlled_buffer_1_out[4], not_7_out, controlled_buffer_1_out[6], controlled_buffer_1_out[7]);
  not not_8 (not_8_out, PA_Bus_En);
  nor nor_1 (Writing_Enable, not_8_out, Writing_Counter_Reset, and_3_out);
  J_K_Flip_Flop j_k_ff_1 (
    .J(Writing_Counter_Reset), .K(and_3_out), .clk(clock_2_out), .Qn(j_k_ff_1_qn));  // open: Q, preset, reset
  Clock clock_2 (.out(clock_2_out));
  nor nor_2 (Custom_Mode_Enabled, j_k_ff_1_qn, PA_Bus_En);
  and and_4 (Default_Mode_Enabled, j_k_ff_1_qn, not_8_out);

  // Notes on the sheet:
  //   AA
  //   DE
endmodule

module Address_Counter (
  input  Reset,
  input  Found,
  output [2:0] Address
);

  wire clock_1_out;
  wire [3:0] register_1_q, rom_1_data;

  Register #(.width(4)) register_1 (.D(rom_1_data), .en(1'b1), .clk(clock_1_out), .Q(register_1_q));  // open: clr
  Clock clock_1 (.out(clock_1_out));
  ROM #(.addrWidth(6), .dataWidth(7)) rom_1 (.addr({Found, Reset, register_1_q}), .data({Address, rom_1_data}));

  // Notes on the sheet:
  //   contents of rom_1 (hex, n*v repeats v):
  //   11 22 33 44 55 66 77 25*0 8 19 2a 3b 4c 5d 6e 7f 8 19 2a 3b 4c 5d 6e 7f
endmodule

module Writing_Counter (
  input  Reset,
  output [2:0] Address
);

  wire clock_1_out;
  wire [2:0] rom_1_data;

  Register #(.width(3)) register_1 (.D(rom_1_data), .en(1'b1), .clk(clock_1_out), .Q(Address));  // open: clr
  Clock clock_1 (.out(clock_1_out));
  ROM #(.addrWidth(4), .dataWidth(3)) rom_1 (.addr({Reset, Address}), .data(rom_1_data));

  // Notes on the sheet:
  //   contents of rom_1 (hex, n*v repeats v):
  //   1 2 3 4 5 6 7
endmodule

module Currently_Handled_Request_Register (
  input  [7:0] CHR_In,
  input  BUS_En,
  input  Reset,
  output [7:0] CHR_Out_BUS
);

  wire clock_1_out;
  wire [7:0] and_1_out, or_1_out, register_1_q;
  wire [7:7] not_1_out;

  not not_1 (not_1_out[7], Reset);
  assign or_1_out = register_1_q | CHR_In;  // OR_Gate or_1, 8 bits wide
  Register register_1 (.D(and_1_out), .en(1'b1), .clk(clock_1_out), .Q(register_1_q));  // open: clr
  assign and_1_out = or_1_out & {8{not_1_out[7]}};  // AND_Gate and_1, 8 bits wide
  Clock clock_1 (.out(clock_1_out));
  assign CHR_Out_BUS = BUS_En ? register_1_q : 8'bz;  // Controlled_Buffer controlled_buffer_1
endmodule

module Program_Controller (
  input  [7:0] PC_In_BUS,
  input  [7:0] DATA_In,
  input  READ,
  input  WRITE,
  input  INT_A,
  output [7:0] DATA_Out,
  output IRR_BUS_En,
  output CHRR_BUS_En,
  output IMR_BUS_En,
  output PA_BUS_En,
  output Reset,
  output [7:0] PC_Out_BUS
);

  wire internal_bus_controller_1_read_out, interrupt_acknowledge_handler_1_int_a_2,
       priority_writing_inspector_1_reset_to_default;

  IR_Vector_to_Interrupt_Number_List_Decoder ir_vector_to_interrupt_number_list_decoder_1 (
    .IRR_BUS_En(IRR_BUS_En), .DATA_Out(DATA_Out), .PC_In_BUS(PC_In_BUS),
    .READ(internal_bus_controller_1_read_out));
  Internal_BUS_Controller internal_bus_controller_1 (
    .PC_Out_BUS(PC_Out_BUS), .Reset(Reset), .READ(READ), .IRR_BUS_En(IRR_BUS_En), .DATA_In(DATA_In),
    .PA_BUS_En(PA_BUS_En), .Reset_To_Default(priority_writing_inspector_1_reset_to_default), .WRITE(WRITE),
    .INT_A_2(interrupt_acknowledge_handler_1_int_a_2), .READ_Out(internal_bus_controller_1_read_out),
    .IMR_BUS_En(IMR_BUS_En), .CHRR_Bus_En(CHRR_BUS_En));
  Priority_Writing_Inspector priority_writing_inspector_1 (
    .Reset_To_Default(priority_writing_inspector_1_reset_to_default), .DATA_In(DATA_In),
    .PC_Out_BUS(PC_Out_BUS), .PA_BUS_En(PA_BUS_En), .DATA_Out(DATA_Out));
  CHR_Vector_to_Interrupt_Number_Decoder chr_vector_to_interrupt_number_decoder_1 (
    .DATA_Out(DATA_Out), .INT_A_2(interrupt_acknowledge_handler_1_int_a_2), .PC_In_BUS(PC_In_BUS));
  Interrupt_Acknowledge_Handler interrupt_acknowledge_handler_1 (
    .INT_A_2(interrupt_acknowledge_handler_1_int_a_2), .INT_A(INT_A));
endmodule

module IR_Vector_to_Interrupt_Number_List_Decoder (
  input  IRR_BUS_En,
  input  [7:0] PC_In_BUS,
  input  READ,
  output [7:0] DATA_Out
);

  wire and_2_out, and_3_out, and_4_out, clock_1_out, clock_2_out, d_ff_1_q, not_1_out, not_3_out, or_1_out,
       or_2_out, xor_1_out;
  wire [2:0] multiplexer_8_out, multiplexer_9_out, multiplexer_11_out, multiplexer_12_out,
       multiplexer_13_out, multiplexer_14_out, multiplexer_15_out, multiplexer_16_out;
  wire [7:0] and_1_out, controlled_buffer_1_out, multiplexer_1_out, multiplexer_2_out, multiplexer_3_out,
       multiplexer_4_out, multiplexer_5_out, multiplexer_6_out, multiplexer_7_out, multiplexer_10_out,
       not_2_out, register_1_q, rom_1_data;

  Multiplexer #(.width(8), .enable("false")) multiplexer_1 (
    .in0({8{1'b0}}), .in1(8'h80), .out(multiplexer_1_out), .sel(register_1_q[7]));
  Multiplexer #(.width(8), .enable("false")) multiplexer_2 (
    .in0(multiplexer_1_out), .in1(8'h40), .out(multiplexer_2_out), .sel(register_1_q[6]));
  Multiplexer #(.width(8), .enable("false")) multiplexer_3 (
    .in0(multiplexer_2_out), .in1(8'h20), .out(multiplexer_3_out), .sel(register_1_q[5]));
  Multiplexer #(.width(8), .enable("false")) multiplexer_4 (
    .in0(multiplexer_3_out), .in1(8'h10), .out(multiplexer_4_out), .sel(register_1_q[4]));
  Multiplexer #(.width(8), .enable("false")) multiplexer_5 (
    .in0(multiplexer_4_out), .in1(8'h8), .out(multiplexer_5_out), .sel(register_1_q[3]));
  Multiplexer #(.width(8), .enable("false")) multiplexer_6 (
    .in0(multiplexer_7_out), .in1(8'h2), .out(multiplexer_6_out), .sel(register_1_q[1]));
  Multiplexer #(.width(8), .enable("false")) multiplexer_7 (
    .in0(multiplexer_5_out), .in1(8'h4), .out(multiplexer_7_out), .sel(register_1_q[2]));
  Multiplexer #(.width(3), .enable("false")) multiplexer_8 (
    .in0(3'b000), .in1(3'b111), .out(multiplexer_8_out), .sel(and_1_out[7]));
  Multiplexer #(.width(3), .enable("false")) multiplexer_9 (
    .in0(multiplexer_8_out), .in1(3'b110), .out(multiplexer_9_out), .sel(and_1_out[6]));
  assign controlled_buffer_1_out = IRR_BUS_En ? PC_In_BUS : 8'bz;  // Controlled_Buffer controlled_buffer_1
  Multiplexer #(.width(8), .enable("false")) multiplexer_10 (
    .in0(multiplexer_6_out), .in1(8'h1), .out(multiplexer_10_out), .sel(register_1_q[0]));
  Multiplexer #(.width(3), .enable("false")) multiplexer_11 (
    .in0(multiplexer_9_out), .in1(3'b101), .out(multiplexer_11_out), .sel(and_1_out[5]));
  not not_1 (not_1_out, IRR_BUS_En);
  assign controlled_buffer_1_out = not_1_out ? register_1_q : 8'bz;  // Controlled_Buffer controlled_buffer_2
  assign and_1_out = controlled_buffer_1_out & not_2_out;  // AND_Gate and_1, 8 bits wide
  assign not_2_out = ~multiplexer_10_out;  // NOT_Gate not_2, 8 bits wide
  Multiplexer #(.width(3), .enable("false")) multiplexer_12 (
    .in0(multiplexer_11_out), .in1(3'b100), .out(multiplexer_12_out), .sel(and_1_out[4]));
  Register register_1 (.D(and_1_out), .en(1'b1), .clk(clock_1_out), .Q(register_1_q));  // open: clr
  Clock clock_1 (.out(clock_1_out));
  Multiplexer #(.width(3), .enable("false")) multiplexer_13 (
    .in0(multiplexer_14_out), .in1(3'b010), .out(multiplexer_13_out), .sel(and_1_out[2]));
  Multiplexer #(.width(3), .enable("false")) multiplexer_14 (
    .in0(multiplexer_12_out), .in1(3'b011), .out(multiplexer_14_out), .sel(and_1_out[3]));
  Multiplexer #(.width(3), .enable("false")) multiplexer_15 (
    .in0(multiplexer_13_out), .in1(3'b001), .out(multiplexer_15_out), .sel(and_1_out[1]));
  ROM #(.addrWidth(3)) rom_1 (.addr(multiplexer_16_out), .data(rom_1_data));
  Multiplexer #(.width(3), .enable("false")) multiplexer_16 (
    .in0(multiplexer_15_out), .in1(3'b000), .out(multiplexer_16_out), .sel(and_1_out[0]));
  or or_1 (or_1_out, and_1_out[0], and_1_out[1], and_1_out[2], and_1_out[3], and_1_out[4], and_1_out[5], and_1_out[6], and_1_out[7]);
  and and_2 (and_2_out, or_1_out, READ);
  xor xor_1 (xor_1_out, IRR_BUS_En, d_ff_1_q);
  assign DATA_Out = and_3_out ? rom_1_data : 8'bz;  // Controlled_Buffer controlled_buffer_3
  D_Flip_Flop d_ff_1 (.D(and_3_out), .clk(clock_2_out), .Q(d_ff_1_q));  // open: Qn, preset, reset
  and and_3 (and_3_out, and_2_out, xor_1_out);
  Clock clock_2 (.out(clock_2_out));
  assign DATA_Out = and_4_out ? {8{1'b0}} : 8'bz;  // Controlled_Buffer controlled_buffer_4
  and and_4 (and_4_out, or_2_out, d_ff_1_q);
  or or_2 (or_2_out, not_3_out, IRR_BUS_En);
  not not_3 (not_3_out, and_2_out);

  // Notes on the sheet:
  //   contents of rom_1 (hex, n*v repeats v):
  //   a0 a1 a2 a3 a4 a5 a6 a7
endmodule

module CHR_Vector_to_Interrupt_Number_Decoder (
  input  [7:0] PC_In_BUS,
  input  INT_A_2,
  output [7:0] DATA_Out
);

  wire not_1_out;
  wire [2:0] multiplexer_1_out, multiplexer_2_out, multiplexer_3_out, multiplexer_4_out, multiplexer_5_out,
       multiplexer_6_out, multiplexer_7_out, multiplexer_8_out;
  wire [7:0] controlled_buffer_1_out, rom_1_data;

  Multiplexer #(.width(3), .enable("false")) multiplexer_1 (
    .in0(3'b000), .in1(3'b111), .out(multiplexer_1_out), .sel(controlled_buffer_1_out[7]));
  Multiplexer #(.width(3), .enable("false")) multiplexer_2 (
    .in0(multiplexer_1_out), .in1(3'b110), .out(multiplexer_2_out), .sel(controlled_buffer_1_out[6]));
  Multiplexer #(.width(3), .enable("false")) multiplexer_3 (
    .in0(multiplexer_2_out), .in1(3'b101), .out(multiplexer_3_out), .sel(controlled_buffer_1_out[5]));
  Multiplexer #(.width(3), .enable("false")) multiplexer_4 (
    .in0(multiplexer_3_out), .in1(3'b100), .out(multiplexer_4_out), .sel(controlled_buffer_1_out[4]));
  Multiplexer #(.width(3), .enable("false")) multiplexer_5 (
    .in0(multiplexer_4_out), .in1(3'b011), .out(multiplexer_5_out), .sel(controlled_buffer_1_out[3]));
  assign controlled_buffer_1_out = not_1_out ? {8{1'b0}} : 8'bz;  // Controlled_Buffer controlled_buffer_1
  assign controlled_buffer_1_out = INT_A_2 ? PC_In_BUS : 8'bz;  // Controlled_Buffer controlled_buffer_2
  not not_1 (not_1_out, INT_A_2);
  Multiplexer #(.width(3), .enable("false")) multiplexer_6 (
    .in0(multiplexer_5_out), .in1(3'b010), .out(multiplexer_6_out), .sel(controlled_buffer_1_out[2]));
  Multiplexer #(.width(3), .enable("false")) multiplexer_7 (
    .in0(multiplexer_6_out), .in1(3'b001), .out(multiplexer_7_out), .sel(controlled_buffer_1_out[1]));
  Multiplexer #(.width(3), .enable("false")) multiplexer_8 (
    .in0(multiplexer_7_out), .in1(3'b000), .out(multiplexer_8_out), .sel(controlled_buffer_1_out[0]));
  ROM #(.addrWidth(3)) rom_1 (.addr(multiplexer_8_out), .data(rom_1_data));
  assign DATA_Out = INT_A_2 ? rom_1_data : 8'bz;  // Controlled_Buffer controlled_buffer_3

  // Notes on the sheet:
  //   contents of rom_1 (hex, n*v repeats v):
  //   a0 a1 a2 a3 a4 a5 a6 a7
endmodule

module Interrupt_Acknowledge_Handler (
  input  INT_A,
  output INT_A_2
);

  wire and_1_out, and_2_out, and_3_out, clock_1_out, clock_2_out, d_ff_1_q, d_ff_1_qn, d_ff_2_q, d_ff_2_qn,
       not_1_out, or_1_out, or_2_out;

  or or_1 (or_1_out, d_ff_2_q, d_ff_1_qn);
  and and_1 (and_1_out, d_ff_2_q, INT_A);
  not not_1 (not_1_out, INT_A);
  and and_2 (and_2_out, not_1_out, d_ff_1_q, d_ff_2_qn);
  and and_3 (and_3_out, INT_A, or_1_out);
  Clock clock_1 (.out(clock_1_out));
  or or_2 (or_2_out, and_1_out, and_2_out);
  Clock clock_2 (.out(clock_2_out));
  D_Flip_Flop d_ff_1 (.D(and_3_out), .clk(clock_1_out), .Q(d_ff_1_q), .Qn(d_ff_1_qn));  // open: preset, reset
  D_Flip_Flop d_ff_2 (.D(or_2_out), .clk(clock_2_out), .Q(d_ff_2_q), .Qn(d_ff_2_qn));  // open: preset, reset
  and and_4 (INT_A_2, d_ff_1_qn, d_ff_2_q, INT_A);
endmodule

module Internal_BUS_Controller (
  input  Reset_To_Default,
  input  READ,
  input  WRITE,
  input  [7:0] DATA_In,
  input  INT_A_2,
  output PA_BUS_En,
  output Reset,
  output IRR_BUS_En,
  output READ_Out,
  output IMR_BUS_En,
  output CHRR_Bus_En,
  output [7:0] PC_Out_BUS
);

  wire and_3_out, and_4_out, and_5_out, and_7_out, and_8_out, and_12_out, and_13_out, clock_1_out,
       clock_2_out, clock_3_out, d_ff_1_qn, d_ff_2_qn, nor_1_out, nor_2_out, nor_3_out, not_1_out, not_2_out,
       not_3_out, not_4_out, not_5_out, not_6_out, not_7_out, not_8_out, not_9_out, not_10_out, not_11_out,
       not_12_out, not_13_out, not_14_out, not_15_out, not_16_out, not_17_out, not_18_out, not_19_out,
       not_20_out, or_1_out, or_2_out, PA_BUS_En_t, WR;
  wire [3:0] register_1_q, rom_1_data;
  wire [6:4] and_9_out;
  wire [7:0] controlled_buffer_1_out;

  not not_1 (not_1_out, WRITE);
  not not_2 (not_2_out, READ);
  and and_1 (READ_Out, not_1_out, READ);
  and and_2 (WR, WRITE, not_2_out);
  assign controlled_buffer_1_out = not_3_out ? {8{1'b0}} : 8'bz;  // Controlled_Buffer controlled_buffer_1
  not not_3 (not_3_out, or_1_out);
  assign controlled_buffer_1_out = or_1_out ? DATA_In : 8'bz;  // Controlled_Buffer controlled_buffer_2
  or or_1 (or_1_out, READ_Out, WR);
  or or_2 (or_2_out, PA_BUS_En_t, IMR_BUS_En);
  assign PC_Out_BUS = or_2_out ? DATA_In : 8'bz;  // Controlled_Buffer controlled_buffer_3
  not not_4 (not_4_out, controlled_buffer_1_out[0]);
  not not_5 (not_5_out, controlled_buffer_1_out[5]);
  not not_6 (not_6_out, controlled_buffer_1_out[0]);
  not not_7 (not_7_out, controlled_buffer_1_out[2]);
  not not_8 (not_8_out, controlled_buffer_1_out[4]);
  not not_9 (not_9_out, controlled_buffer_1_out[6]);
  not not_10 (not_10_out, controlled_buffer_1_out[0]);
  not not_11 (not_11_out, controlled_buffer_1_out[2]);
  not not_12 (not_12_out, controlled_buffer_1_out[5]);
  not not_13 (not_13_out, controlled_buffer_1_out[2]);
  not not_14 (not_14_out, controlled_buffer_1_out[5]);
  not not_15 (not_15_out, controlled_buffer_1_out[0]);
  not not_16 (not_16_out, controlled_buffer_1_out[1]);
  not not_17 (not_17_out, controlled_buffer_1_out[4]);
  not not_18 (not_18_out, controlled_buffer_1_out[5]);
  not not_19 (not_19_out, controlled_buffer_1_out[2]);
  not not_20 (not_20_out, controlled_buffer_1_out[6]);
  and and_3 (and_3_out, not_4_out, controlled_buffer_1_out[1], controlled_buffer_1_out[2], controlled_buffer_1_out[3], controlled_buffer_1_out[4], not_5_out, controlled_buffer_1_out[6], controlled_buffer_1_out[7]);
  and and_4 (and_4_out, not_6_out, controlled_buffer_1_out[1], not_7_out, controlled_buffer_1_out[3], not_8_out, controlled_buffer_1_out[5], not_9_out, controlled_buffer_1_out[7]);
  and and_5 (and_5_out, not_10_out, controlled_buffer_1_out[1], not_11_out, controlled_buffer_1_out[3], controlled_buffer_1_out[4], not_12_out, controlled_buffer_1_out[6], controlled_buffer_1_out[7]);
  and and_6 (Reset, controlled_buffer_1_out[0], controlled_buffer_1_out[1], not_13_out, controlled_buffer_1_out[3], controlled_buffer_1_out[4], not_14_out, controlled_buffer_1_out[6], controlled_buffer_1_out[7]);
  and and_7 (and_7_out, not_15_out, not_16_out, controlled_buffer_1_out[2], controlled_buffer_1_out[3], not_17_out, not_18_out, controlled_buffer_1_out[6], controlled_buffer_1_out[7]);
  and and_8 (and_8_out, controlled_buffer_1_out[0], controlled_buffer_1_out[1], not_19_out, controlled_buffer_1_out[3], controlled_buffer_1_out[4], controlled_buffer_1_out[5], not_20_out, controlled_buffer_1_out[7]);
  Register #(.width(4)) register_1 (.D(rom_1_data), .en(1'b1), .clk(clock_1_out), .Q(register_1_q));  // open: clr
  Clock clock_1 (.out(clock_1_out));
  and and_9 (and_9_out[4], WR, and_3_out);
  and and_10 (and_9_out[5], WR, and_4_out);
  and and_11 (and_9_out[6], WR, and_5_out);
  nor nor_1 (nor_1_out, CHRR_Bus_En, PA_BUS_En_t, IMR_BUS_En);
  nor nor_2 (nor_2_out, CHRR_Bus_En, PA_BUS_En_t, IRR_BUS_En);
  nor nor_3 (nor_3_out, IMR_BUS_En, PA_BUS_En_t, IRR_BUS_En);
  ROM #(.addrWidth(7), .dataWidth(5)) rom_1 (.addr({and_9_out, register_1_q}), .data({PA_BUS_En_t, rom_1_data}));
  and and_12 (and_12_out, READ_Out, and_7_out, nor_1_out, d_ff_1_qn);
  Clock clock_2 (.out(clock_2_out));
  and and_13 (and_13_out, WR, and_8_out, nor_2_out, d_ff_2_qn);
  Clock clock_3 (.out(clock_3_out));
  and and_14 (CHRR_Bus_En, INT_A_2, nor_3_out);
  D_Flip_Flop d_ff_1 (.D(and_12_out), .clk(clock_2_out), .Q(IRR_BUS_En), .Qn(d_ff_1_qn));  // open: preset, reset
  D_Flip_Flop d_ff_2 (.D(and_13_out), .clk(clock_3_out), .Q(IMR_BUS_En), .Qn(d_ff_2_qn));  // open: preset, reset
  or or_3 (PA_BUS_En, PA_BUS_En_t, Reset_To_Default);

  // Other names for the same wires on the sheet: RE = READ_Out

  // Notes on the sheet:
  //   DE
  //   AA
  //   DA
  //   DB
  //   CC
  //   BB
  //   contents of rom_1 (hex, n*v repeats v):
  //   0 0 13 14 15 16 17 18 19 10 7*0 10 13 14 15 16 17 18 19 10 7*0 12 13 14 15 16 17 18 19 10 8*0 13 14
  //   15 16 17 18 19 10 6*0 1 0 13 14 15 16 17 18 19 10 8*0 13 14 15 16 17 18 19 10 8*0 13 14 15 16 17 18
  //   19 10 8*0 13 14 15 16 17 18 19 10
endmodule

module Priority_Writing_Inspector (
  input  [7:0] DATA_In,
  input  PA_BUS_En,
  output [7:0] DATA_Out,
  output [7:0] PC_Out_BUS,
  output Reset_To_Default
);

  wire and_2_out, and_4_out, clock_1_out, clock_2_out, clock_3_out, clock_4_out, comparator_1_eq,
       counter_0_8_1_end_of_cnt, d_ff_1_q, d_ff_2_q, d_ff_2_qn, nand_1_out, not_1_out, not_3_out, or_1_out,
       valid_word_detector_1_invalid;
  wire [7:0] and_1_out, controlled_buffer_1_out, register_1_q, xor_1_out;
  wire [7:4] and_3_out;
  wire [7:7] not_2_out;

  assign controlled_buffer_1_out = PA_BUS_En ? DATA_In : 8'bz;  // Controlled_Buffer controlled_buffer_1
  not not_1 (not_1_out, PA_BUS_En);
  assign controlled_buffer_1_out = not_1_out ? {8{1'b0}} : 8'bz;  // Controlled_Buffer controlled_buffer_2
  assign xor_1_out = register_1_q ^ controlled_buffer_1_out;  // XOR_Gate xor_1, 8 bits wide
  Register register_1 (.D(and_1_out), .en(1'b1), .clk(clock_1_out), .Q(register_1_q));  // open: clr
  assign and_1_out = xor_1_out & {8{not_2_out[7]}};  // AND_Gate and_1, 8 bits wide
  Clock clock_1 (.out(clock_1_out));
  not not_2 (not_2_out[7], nand_1_out);
  Clock clock_2 (.out(clock_2_out));
  Valid_Word_Detector valid_word_detector_1 (.Word(controlled_buffer_1_out), .Invalid(valid_word_detector_1_invalid));
  D_Flip_Flop d_ff_1 (.D(PA_BUS_En), .clk(clock_2_out), .Q(d_ff_1_q));  // open: Qn, preset, reset
  or or_1 (or_1_out, d_ff_2_q, valid_word_detector_1_invalid);
  not not_3 (not_3_out, nand_1_out);
  Comparator comparator_1 (.a(register_1_q), .b({8{1'b1}}), .eq(comparator_1_eq));  // open: gt, lt
  nand nand_1 (nand_1_out, PA_BUS_En, d_ff_1_q);
  D_Flip_Flop d_ff_2 (.D(and_2_out), .clk(clock_3_out), .Q(d_ff_2_q), .Qn(d_ff_2_qn));  // open: preset, reset
  and and_2 (and_2_out, or_1_out, not_3_out);
  Clock clock_3 (.out(clock_3_out));
  Counter_0_8 counter_0_8_1 (.RST(nand_1_out), .End_Of_CNT(counter_0_8_1_end_of_cnt));
  assign DATA_Out = counter_0_8_1_end_of_cnt ? {{3{and_3_out[7]}}, and_3_out[4], {3{and_3_out[7]}}, and_3_out[4]} : 8'bz;  // Controlled_Buffer controlled_buffer_3
  not not_4 (and_3_out[7], and_3_out[4]);
  and and_3 (and_3_out[4], d_ff_2_qn, comparator_1_eq, counter_0_8_1_end_of_cnt);
  and and_4 (and_4_out, and_3_out[7], counter_0_8_1_end_of_cnt);
  D_Flip_Flop d_ff_3 (.D(and_4_out), .clk(clock_4_out), .Q(Reset_To_Default));  // open: Qn, preset, reset
  Clock clock_4 (.out(clock_4_out));
  assign PC_Out_BUS = Reset_To_Default ? 8'hde : 8'bz;  // Controlled_Buffer controlled_buffer_4

  // Notes on the sheet:
  //   All the words are different Detector
  //   11 - Valid list
  //   EE - ERROR in the list
  //   Default when ERROR
endmodule

module Counter_0_8 (
  input  RST,
  output End_Of_CNT
);

  wire clock_1_out;
  wire [3:0] register_1_q, rom_1_data;

  Register #(.width(4)) register_1 (.D(rom_1_data), .en(1'b1), .clk(clock_1_out), .Q(register_1_q));  // open: clr
  Clock clock_1 (.out(clock_1_out));
  ROM #(.addrWidth(5), .dataWidth(5)) rom_1 (.addr({RST, register_1_q}), .data({End_Of_CNT, rom_1_data}));

  // Notes on the sheet:
  //   contents of rom_1 (hex, n*v repeats v):
  //   1 2 3 4 5 6 7 8 10 15*0 10
endmodule

module Valid_Word_Detector (
  input  [7:0] Word,
  output Invalid
);

  wire and_1_out, and_2_out, and_3_out, and_4_out, and_5_out, and_6_out, and_7_out, and_8_out, and_9_out,
       and_10_out, not_1_out, or_1_out, or_2_out, or_3_out, xor_1_out, xor_2_out, xor_3_out, xor_4_out;

  and and_1 (and_1_out, Word[0], Word[1]);
  and and_2 (and_2_out, Word[0], Word[2]);
  or or_1 (or_1_out, and_1_out, and_2_out, and_3_out);
  and and_3 (and_3_out, Word[1], Word[2]);
  ExactlyOne xor_1 (.out(xor_1_out), .in0(Word[0]), .in1(Word[1]), .in2(Word[2]));
  ExactlyOne xor_2 (.out(xor_2_out), .in0(Word[3]), .in1(Word[4]), .in2(Word[5]));
  xor xor_3 (xor_3_out, Word[6], Word[7]);
  and and_4 (and_4_out, Word[3], Word[4]);
  and and_5 (and_5_out, Word[3], Word[5]);
  or or_2 (or_2_out, and_4_out, and_5_out, and_6_out);
  and and_6 (and_6_out, Word[4], Word[5]);
  and and_7 (and_7_out, Word[6], Word[7]);
  not not_1 (not_1_out, xor_4_out);
  ExactlyOne xor_4 (.out(xor_4_out), .in0(xor_1_out), .in1(xor_2_out), .in2(xor_3_out));
  and and_8 (and_8_out, xor_1_out, xor_2_out);
  and and_9 (and_9_out, xor_1_out, xor_3_out);
  or or_3 (or_3_out, and_8_out, and_9_out, and_10_out);
  and and_10 (and_10_out, xor_3_out, xor_2_out);
  or or_4 (Invalid, or_1_out, not_1_out, or_3_out, or_2_out, and_7_out);
endmodule

module CPU (
  input  [7:0] DATA_In,
  input  INT_A_In,
  input  INT,
  input  [7:0] READ_IO,
  input  set_PA_default,
  input  write_to_PA,
  input  [7:0] PA_List_In,
  input  [7:0] MASK_In,
  input  write_MASK,
  input  read_IRR,
  output INT_A,
  output READ,
  output WRITE,
  output CPU_Busy,
  output [7:0] DATA_Out,
  output [7:0] Address,
  output Reset_CNT,
  output [7:0] WRITE_IO,
  output ROM_En,
  output RAM_En,
  output PA_ERROR,
  output PA_success,
  output Reset_PA_CNT,
  output Reset_IRR_CTR,
  output IRR_RAM_En,
  output [7:0] IRR_RAM_Out
);

  wire A_00, AA, ADD_Reset, and_1_out, and_4_out, and_5_out, and_6_out, and_11_out, and_12_out, and_14_out,
       and_15_out, and_16_out, and_17_out, and_18_out, and_19_out, and_21_out, and_22_out, and_23_out,
       Busy_INT, Busy_IRR, Busy_MASK, Busy_PA, Busy_Req_Reset, Busy_talk_IO, clock_1_out, clock_2_out,
       clock_3_out, clock_4_out, clock_5_out, clock_6_out, clock_7_out, clock_8_out, clock_9_out,
       clock_10_out, clock_11_out, clock_12_out, clock_13_out, clock_14_out, clock_15_out, clock_16_out,
       clock_17_out, clock_18_out, clock_19_out, clock_20_out, clock_21_out, clock_22_out, clock_23_out,
       clock_24_out, D_00, D_11, D_55, D_66, D_77, D_99, D_AC, D_BB, D_EE, d_ff_1_q, d_ff_3_q, d_ff_6_q,
       d_ff_6_qn, d_ff_7_q, d_ff_7_qn, d_ff_15_q, d_ff_15_qn, d_ff_16_q, d_ff_16_qn, INT_A_2, INT_DATA_In_En,
       INT_Sys_Busy, IO_Sys_Busy, IRR_DATA_Out_En, IRR_Sys_Busy, MASK_DATA_Out_En, MASK_Sys_Busy, nor_1_out,
       nor_3_out, not_1_out, not_2_out, not_3_out, not_4_out, not_5_out, not_6_out, not_7_out, not_9_out,
       not_10_out, not_11_out, not_12_out, not_13_out, not_14_out, not_15_out, not_16_out, not_17_out,
       not_18_out, not_19_out, not_20_out, not_21_out, not_22_out, not_23_out, not_24_out, not_25_out,
       not_26_out, not_27_out, not_28_out, not_29_out, not_30_out, not_31_out, not_32_out, not_33_out,
       not_34_out, not_35_out, not_36_out, not_37_out, not_38_out, not_39_out, not_40_out, not_41_out,
       not_42_out, not_43_out, not_44_out, not_45_out, not_46_out, or_1_out, or_3_out, or_6_out, or_7_out,
       or_8_out, or_9_out, or_10_out, or_11_out, or_12_out, Out_DATA_ADD_En, PA_DATA_In_En, PA_DATA_Out_En,
       PA_Sys_Busy, por_1_out, por_2_out, por_3_out, por_4_out, por_5_out, Req_Reset_Out_En, Start_IO,
       talk_IO_DATA_In_En, WORD_bit_1, WORD_bit_2, WRITE_MASK_t, WRITE_PA;
  wire [1:0] register_2_q, register_5_q, rom_4_data, rom_5_data;
  wire [2:0] register_3_q, register_4_q, register_7_q, rom_1_data, rom_2_data, rom_6_data;
  wire [3:0] controlled_buffer_1_out, register_1_q, rom_3_data;
  wire [4:0] controlled_buffer_3_out;
  wire [6:0] controlled_buffer_4_out;
  wire [6:5] and_9_out;
  wire [7:0] and_3_out, controlled_buffer_6_out, controlled_buffer_11_out, controlled_buffer_16_out,
       controlled_buffer_18_out, controlled_buffer_20_out, controlled_buffer_22_out,
       controlled_buffer_25_out, controlled_buffer_27_out, controlled_buffer_31_out,
       controlled_buffer_34_out, register_6_q;
  wire [7:7] not_8_out;
  wire [8:0] controlled_buffer_8_out;

  Clock clock_1 (.out(clock_1_out));
  Register #(.width(4)) register_1 (.D(rom_3_data), .en(1'b1), .clk(clock_2_out), .Q(register_1_q));  // open: clr
  Clock clock_2 (.out(clock_2_out));
  Register #(.width(2)) register_2 (.D(rom_4_data), .en(1'b1), .clk(clock_3_out), .Q(register_2_q));  // open: clr
  Clock clock_3 (.out(clock_3_out));
  Clock clock_4 (.out(clock_4_out));
  Register #(.width(3)) register_3 (.D(rom_1_data), .en(1'b1), .clk(clock_5_out), .Q(register_3_q));  // open: clr
  Clock clock_5 (.out(clock_5_out));
  Register #(.width(3)) register_4 (.D(rom_2_data), .en(1'b1), .clk(clock_1_out), .Q(register_4_q));  // open: clr
  Register #(.width(2)) register_5 (.D(rom_5_data), .en(1'b1), .clk(clock_4_out), .Q(register_5_q));  // open: clr
  or or_1 (or_1_out, Reset_CNT, d_ff_1_q);
  POR por_1 (.out(por_1_out));
  POR por_2 (.out(por_2_out));
  assign controlled_buffer_1_out = not_1_out ? {write_MASK, Busy_MASK, register_2_q} : 4'bz;  // Controlled_Buffer controlled_buffer_1
  not not_1 (not_1_out, por_3_out);
  assign controlled_buffer_1_out = por_3_out ? 4'b0000 : 4'bz;  // Controlled_Buffer controlled_buffer_2
  POR por_3 (.out(por_3_out));
  assign controlled_buffer_3_out = not_2_out ? {read_IRR, Busy_IRR, A_00, register_5_q} : 5'bz;  // Controlled_Buffer controlled_buffer_3
  not not_2 (not_2_out, por_4_out);
  POR por_4 (.out(por_4_out));
  and and_1 (and_1_out, Busy_Req_Reset, or_1_out);
  and and_2 (Req_Reset_Out_En, or_1_out, not_3_out);
  not not_3 (not_3_out, Busy_Req_Reset);
  ROM #(.addrWidth(7), .dataWidth(7)) rom_1 (
    .addr(controlled_buffer_4_out), .data({Start_IO, INT_A, INT_Sys_Busy, INT_DATA_In_En, rom_1_data}));
  assign controlled_buffer_4_out = not_4_out ? {INT, INT_A_In, D_00, Busy_INT, register_3_q} : 7'bz;  // Controlled_Buffer controlled_buffer_4
  not not_4 (not_4_out, por_5_out);
  assign controlled_buffer_4_out = por_5_out ? {7{1'b0}} : 7'bz;  // Controlled_Buffer controlled_buffer_5
  POR por_5 (.out(por_5_out));
  ROM #(.dataWidth(9)) rom_2 (
    .addr(controlled_buffer_6_out),
    .data({D_77, D_AC, IO_Sys_Busy, talk_IO_DATA_In_En, Out_DATA_ADD_En, ADD_Reset, rom_2_data}));
  assign controlled_buffer_6_out = not_5_out ? {Start_IO, D_66, D_99, Reset_CNT, Busy_talk_IO, register_4_q} : 8'bz;  // Controlled_Buffer controlled_buffer_6
  not not_5 (not_5_out, por_1_out);
  assign controlled_buffer_6_out = por_1_out ? {8{1'b0}} : 8'bz;  // Controlled_Buffer controlled_buffer_7
  ROM #(.addrWidth(9), .dataWidth(12)) rom_3 (
    .addr(controlled_buffer_8_out),
    .data({PA_DATA_Out_En, PA_DATA_In_En, PA_success, PA_ERROR, WRITE_PA, PA_Sys_Busy, WORD_bit_1, WORD_bit_2, rom_3_data}));
  assign controlled_buffer_8_out = not_6_out ? {write_to_PA, set_PA_default, D_EE, D_11, Busy_PA, register_1_q} : 9'bz;  // Controlled_Buffer controlled_buffer_8
  not not_6 (not_6_out, por_2_out);
  assign controlled_buffer_8_out = por_2_out ? {9{1'b0}} : 9'bz;  // Controlled_Buffer controlled_buffer_9
  ROM #(.addrWidth(4), .dataWidth(6)) rom_4 (
    .addr(controlled_buffer_1_out), .data({WRITE_MASK_t, MASK_Sys_Busy, MASK_DATA_Out_En, D_BB, rom_4_data}));
  ROM #(.addrWidth(5), .dataWidth(7)) rom_5 (
    .addr(controlled_buffer_3_out),
    .data({READ, IRR_Sys_Busy, IRR_RAM_En, IRR_DATA_Out_En, Reset_IRR_CTR, rom_5_data}));
  assign controlled_buffer_3_out = por_4_out ? {5{1'b0}} : 5'bz;  // Controlled_Buffer controlled_buffer_10
  D_Flip_Flop d_ff_1 (.D(and_1_out), .clk(clock_6_out), .Q(d_ff_1_q));  // open: Qn, preset, reset
  Clock clock_6 (.out(clock_6_out));
  or or_2 (Busy_Req_Reset, INT_Sys_Busy, IO_Sys_Busy, IRR_Sys_Busy, PA_Sys_Busy, MASK_Sys_Busy);
  not not_7 (not_7_out, INT_A_2);
  assign controlled_buffer_11_out = not_7_out ? register_6_q : 8'bz;  // Controlled_Buffer controlled_buffer_11
  assign controlled_buffer_11_out = INT_A_2 ? DATA_In : 8'bz;  // Controlled_Buffer controlled_buffer_12
  not not_8 (not_8_out[7], ADD_Reset);
  or or_3 (or_3_out, INT_Sys_Busy, PA_Sys_Busy, Req_Reset_Out_En, MASK_Sys_Busy, IRR_Sys_Busy);
  Clock clock_7 (.out(clock_7_out));
  Register register_6 (.D(and_3_out), .en(1'b1), .clk(clock_8_out), .Q(register_6_q));  // open: clr
  assign and_3_out = controlled_buffer_11_out & {8{not_8_out[7]}};  // AND_Gate and_3, 8 bits wide
  Clock clock_8 (.out(clock_8_out));
  D_Flip_Flop d_ff_2 (.D(or_3_out), .clk(clock_7_out), .Q(Busy_talk_IO));  // open: Qn, preset, reset
  assign DATA_Out = Req_Reset_Out_En ? 8'hdb : 8'bz;  // Controlled_Buffer controlled_buffer_13
  D_Flip_Flop d_ff_3 (.D(INT_Sys_Busy), .clk(clock_9_out), .Q(d_ff_3_q));  // open: Qn, preset, reset
  Clock clock_9 (.out(clock_9_out));
  or or_4 (WRITE, WRITE_PA, Req_Reset_Out_En, WRITE_MASK_t);
  or or_5 (CPU_Busy, IO_Sys_Busy, PA_Sys_Busy, INT_Sys_Busy, Req_Reset_Out_En, MASK_Sys_Busy, IRR_Sys_Busy, d_ff_3_q);
  not not_9 (not_9_out, Out_DATA_ADD_En);
  assign Address = Out_DATA_ADD_En ? register_6_q : 8'bz;  // Controlled_Buffer controlled_buffer_14
  assign Address = not_9_out ? {8{1'b0}} : 8'bz;  // Controlled_Buffer controlled_buffer_15
  assign controlled_buffer_16_out = talk_IO_DATA_In_En ? DATA_In : 8'bz;  // Controlled_Buffer controlled_buffer_16
  assign controlled_buffer_16_out = Out_DATA_ADD_En ? DATA_Out : 8'bz;  // Controlled_Buffer controlled_buffer_17
  assign controlled_buffer_18_out = talk_IO_DATA_In_En ? DATA_In : 8'bz;  // Controlled_Buffer controlled_buffer_18
  not not_10 (not_10_out, talk_IO_DATA_In_En);
  assign controlled_buffer_18_out = not_10_out ? {8{1'b1}} : 8'bz;  // Controlled_Buffer controlled_buffer_19
  assign controlled_buffer_20_out = D_77 ? 8'h77 : 8'bz;  // Controlled_Buffer controlled_buffer_20
  assign controlled_buffer_20_out = D_AC ? 8'hac : 8'bz;  // Controlled_Buffer controlled_buffer_21
  assign controlled_buffer_22_out = INT_DATA_In_En ? DATA_In : 8'bz;  // Controlled_Buffer controlled_buffer_22
  not not_11 (not_11_out, INT_DATA_In_En);
  assign controlled_buffer_22_out = not_11_out ? {8{1'b1}} : 8'bz;  // Controlled_Buffer controlled_buffer_23
  or or_6 (or_6_out, IO_Sys_Busy, PA_Sys_Busy, Req_Reset_Out_En, MASK_Sys_Busy, IRR_Sys_Busy);
  Clock clock_10 (.out(clock_10_out));
  // Probe on controlled_buffer_16_out
  assign DATA_Out = Out_DATA_ADD_En ? controlled_buffer_20_out : 8'bz;  // Controlled_Buffer controlled_buffer_24
  assign controlled_buffer_25_out = PA_DATA_In_En ? DATA_In : 8'bz;  // Controlled_Buffer controlled_buffer_25
  not not_12 (not_12_out, PA_DATA_In_En);
  assign controlled_buffer_25_out = not_12_out ? {8{1'b1}} : 8'bz;  // Controlled_Buffer controlled_buffer_26
  assign controlled_buffer_27_out = D_BB ? 8'hbb : 8'bz;  // Controlled_Buffer controlled_buffer_27
  not not_13 (not_13_out, D_BB);
  assign controlled_buffer_27_out = not_13_out ? MASK_In : 8'bz;  // Controlled_Buffer controlled_buffer_28
  assign IRR_RAM_Out = IRR_RAM_En ? DATA_In : 8'bz;  // Controlled_Buffer controlled_buffer_29
  not not_14 (not_14_out, IRR_RAM_En);
  assign IRR_RAM_Out = not_14_out ? {8{1'b1}} : 8'bz;  // Controlled_Buffer controlled_buffer_30
  assign controlled_buffer_31_out = Reset_IRR_CTR ? 8'hcc : 8'bz;  // Controlled_Buffer controlled_buffer_31
  or or_7 (or_7_out, d_ff_7_q, d_ff_6_qn);
  and and_4 (and_4_out, d_ff_7_q, INT_A);
  not not_15 (not_15_out, INT_A);
  and and_5 (and_5_out, not_15_out, d_ff_6_q, d_ff_7_qn);
  D_Flip_Flop d_ff_4 (.D(or_6_out), .clk(clock_10_out), .Q(Busy_INT));  // open: Qn, preset, reset
  not not_16 (not_16_out, controlled_buffer_16_out[0]);
  not not_17 (not_17_out, controlled_buffer_16_out[2]);
  not not_18 (not_18_out, controlled_buffer_16_out[4]);
  not not_19 (not_19_out, controlled_buffer_16_out[6]);
  not not_20 (not_20_out, controlled_buffer_16_out[1]);
  not not_21 (not_21_out, controlled_buffer_16_out[3]);
  not not_22 (not_22_out, controlled_buffer_16_out[5]);
  not not_23 (not_23_out, controlled_buffer_16_out[7]);
  not not_24 (not_24_out, controlled_buffer_18_out[1]);
  not not_25 (not_25_out, controlled_buffer_18_out[2]);
  not not_26 (not_26_out, controlled_buffer_18_out[5]);
  not not_27 (not_27_out, controlled_buffer_18_out[6]);
  not not_28 (not_28_out, controlled_buffer_18_out[0]);
  not not_29 (not_29_out, controlled_buffer_18_out[3]);
  not not_30 (not_30_out, controlled_buffer_18_out[4]);
  not not_31 (not_31_out, controlled_buffer_18_out[7]);
  assign DATA_Out = IRR_DATA_Out_En ? controlled_buffer_31_out : 8'bz;  // Controlled_Buffer controlled_buffer_32
  D_Flip_Flop d_ff_5 (.D(or_8_out), .clk(clock_11_out), .Q(Busy_IRR));  // open: Qn, preset, reset
  or or_8 (or_8_out, INT_Sys_Busy, IO_Sys_Busy, Req_Reset_Out_En, PA_Sys_Busy, MASK_Sys_Busy);
  Clock clock_11 (.out(clock_11_out));
  D_Flip_Flop d_ff_6 (.D(and_6_out), .clk(clock_12_out), .Q(d_ff_6_q), .Qn(d_ff_6_qn));  // open: preset, reset
  and and_6 (and_6_out, INT_A, or_7_out);
  Clock clock_12 (.out(clock_12_out));
  D_Flip_Flop d_ff_7 (.D(or_9_out), .clk(clock_13_out), .Q(d_ff_7_q), .Qn(d_ff_7_qn));  // open: preset, reset
  or or_9 (or_9_out, and_4_out, and_5_out);
  Clock clock_13 (.out(clock_13_out));
  D_Flip_Flop d_ff_8 (.D(nor_1_out), .clk(clock_14_out), .Q(D_00));  // open: Qn, preset, reset
  nor nor_1 (nor_1_out, controlled_buffer_22_out[0], controlled_buffer_22_out[1], controlled_buffer_22_out[2], controlled_buffer_22_out[3], controlled_buffer_22_out[4], controlled_buffer_22_out[5], controlled_buffer_22_out[6], controlled_buffer_22_out[7]);
  Clock clock_14 (.out(clock_14_out));
  and and_7 (AA, not_16_out, controlled_buffer_16_out[1], not_17_out, controlled_buffer_16_out[3], not_18_out, controlled_buffer_16_out[5], not_19_out, controlled_buffer_16_out[7]);
  and and_8 (D_55, controlled_buffer_16_out[0], not_20_out, controlled_buffer_16_out[2], not_21_out, controlled_buffer_16_out[4], not_22_out, controlled_buffer_16_out[6], not_23_out);
  and and_9 (and_9_out[5], controlled_buffer_18_out[0], not_24_out, not_25_out, controlled_buffer_18_out[3], controlled_buffer_18_out[4], not_26_out, not_27_out, controlled_buffer_18_out[7]);
  and and_10 (and_9_out[6], not_28_out, controlled_buffer_18_out[1], controlled_buffer_18_out[2], not_29_out, not_30_out, controlled_buffer_18_out[5], controlled_buffer_18_out[6], not_31_out);
  not not_32 (not_32_out, controlled_buffer_25_out[1]);
  not not_33 (not_33_out, controlled_buffer_25_out[2]);
  not not_34 (not_34_out, controlled_buffer_25_out[3]);
  not not_35 (not_35_out, controlled_buffer_25_out[5]);
  not not_36 (not_36_out, controlled_buffer_25_out[6]);
  not not_37 (not_37_out, controlled_buffer_25_out[7]);
  not not_38 (not_38_out, controlled_buffer_25_out[0]);
  not not_39 (not_39_out, controlled_buffer_25_out[4]);
  or or_10 (or_10_out, INT_Sys_Busy, IO_Sys_Busy, Req_Reset_Out_En, MASK_Sys_Busy, IRR_Sys_Busy);
  Clock clock_15 (.out(clock_15_out));
  assign DATA_Out = MASK_DATA_Out_En ? controlled_buffer_27_out : 8'bz;  // Controlled_Buffer controlled_buffer_33
  D_Flip_Flop d_ff_9 (.D(or_11_out), .clk(clock_16_out), .Q(Busy_MASK));  // open: Qn, preset, reset
  or or_11 (or_11_out, INT_Sys_Busy, IO_Sys_Busy, Req_Reset_Out_En, PA_Sys_Busy, IRR_Sys_Busy);
  Clock clock_16 (.out(clock_16_out));
  D_Flip_Flop d_ff_10 (.D(and_9_out[5]), .clk(clock_17_out), .Q(D_99));  // open: Qn, preset, reset
  Clock clock_17 (.out(clock_17_out));
  D_Flip_Flop d_ff_11 (.D(and_9_out[6]), .clk(clock_18_out), .Q(D_66));  // open: Qn, preset, reset
  Clock clock_18 (.out(clock_18_out));
  and and_11 (and_11_out, controlled_buffer_25_out[0], not_32_out, not_33_out, not_34_out, controlled_buffer_25_out[4], not_35_out, not_36_out, not_37_out);
  Clock clock_19 (.out(clock_19_out));
  and and_12 (and_12_out, not_38_out, controlled_buffer_25_out[1], controlled_buffer_25_out[2], controlled_buffer_25_out[3], not_39_out, controlled_buffer_25_out[5], controlled_buffer_25_out[6], controlled_buffer_25_out[7]);
  Clock clock_20 (.out(clock_20_out));
  D_Flip_Flop d_ff_12 (.D(or_10_out), .clk(clock_15_out), .Q(Busy_PA));  // open: Qn, preset, reset
  nor nor_2 (A_00, IRR_RAM_Out[0], IRR_RAM_Out[1], IRR_RAM_Out[2], IRR_RAM_Out[3], IRR_RAM_Out[4], IRR_RAM_Out[5], IRR_RAM_Out[6], IRR_RAM_Out[7]);
  D_Flip_Flop d_ff_13 (.D(and_11_out), .clk(clock_19_out), .Q(D_11));  // open: Qn, preset, reset
  D_Flip_Flop d_ff_14 (.D(and_12_out), .clk(clock_20_out), .Q(D_EE));  // open: Qn, preset, reset
  and and_13 (INT_A_2, d_ff_6_qn, d_ff_7_q, INT_A);
  and and_14 (and_14_out, d_ff_16_q, d_ff_15_qn, not_40_out, AA);
  not not_40 (not_40_out, D_55);
  and and_15 (and_15_out, d_ff_15_qn, AA, not_41_out);
  not not_41 (not_41_out, D_55);
  Clock clock_21 (.out(clock_21_out));
  or or_12 (or_12_out, and_14_out, and_16_out);
  Clock clock_22 (.out(clock_22_out));
  and and_16 (and_16_out, D_55, not_42_out, d_ff_15_q, d_ff_16_qn);
  not not_42 (not_42_out, AA);
  D_Flip_Flop d_ff_15 (.D(and_15_out), .clk(clock_21_out), .Q(d_ff_15_q), .Qn(d_ff_15_qn));  // open: preset, reset
  D_Flip_Flop d_ff_16 (.D(or_12_out), .clk(clock_22_out), .Q(d_ff_16_q), .Qn(d_ff_16_qn));  // open: preset, reset
  not not_43 (not_43_out, WORD_bit_2);
  and and_17 (and_17_out, WORD_bit_2, WORD_bit_1);
  and and_18 (and_18_out, WORD_bit_2, not_44_out);
  not not_44 (not_44_out, WORD_bit_1);
  not not_45 (not_45_out, WORD_bit_2);
  and and_19 (and_19_out, not_45_out, WORD_bit_1);
  nor nor_3 (nor_3_out, WORD_bit_2, WORD_bit_1);
  and and_20 (Reset_PA_CNT, not_43_out, WORD_bit_1);
  and and_21 (and_21_out, d_ff_15_q, d_ff_16_q, D_55, not_46_out);
  not not_46 (not_46_out, AA);
  Clock clock_23 (.out(clock_23_out));
  assign controlled_buffer_34_out = and_17_out ? 8'hda : 8'bz;  // Controlled_Buffer controlled_buffer_34
  assign controlled_buffer_34_out = and_18_out ? 8'hde : 8'bz;  // Controlled_Buffer controlled_buffer_35
  assign controlled_buffer_34_out = and_19_out ? 8'haa : 8'bz;  // Controlled_Buffer controlled_buffer_36
  assign controlled_buffer_34_out = nor_3_out ? PA_List_In : 8'bz;  // Controlled_Buffer controlled_buffer_37
  D_Flip_Flop d_ff_17 (.D(and_21_out), .clk(clock_23_out), .Q(Reset_CNT));  // open: Qn, preset, reset
  Register #(.width(3)) register_7 (.D(rom_6_data), .en(1'b1), .clk(clock_24_out), .Q(register_7_q));  // open: clr
  Clock clock_24 (.out(clock_24_out));
  assign DATA_Out = PA_DATA_Out_En ? controlled_buffer_34_out : 8'bz;  // Controlled_Buffer controlled_buffer_38
  ROM #(.addrWidth(7), .dataWidth(5)) rom_6 (
    .addr({and_9_out, D_AC, Reset_CNT, register_7_q}), .data({RAM_En, ROM_En, rom_6_data}));
  assign DATA_Out = and_23_out ? READ_IO : 8'bz;  // Controlled_Buffer controlled_buffer_39
  assign WRITE_IO = and_22_out ? DATA_In : 8'bz;  // Controlled_Buffer controlled_buffer_40
  and and_22 (and_22_out, RAM_En, talk_IO_DATA_In_En);
  and and_23 (and_23_out, ROM_En, Out_DATA_ADD_En);

  // Other names for the same wires on the sheet: D_CC = Reset_IRR_CTR; IRR_DATA_In_En = IRR_RAM_En; EOP = Reset_CNT

  // Notes on the sheet:
  //   contents of rom_1 (hex, n*v repeats v):
  //   0 0 13 3c 40 7*0 40 5*0 13 0 40 7*0 40 4*0 32 13 3c 40 7*0 40 4*0 32 13 0 40 7*0 40 0 0 0 1 1 13 3c
  //   40 0 0 0 1 1 0 0 40 0 0 0 1 1 13 0 40 0 0 0 1 1 0 0 40 0 0 0 1 32 13 3c 40 0 0 0 1 1 0 0 40 0 0 0 1
  //   32 13 0 40 0 0 0 1 1 0 0 40
  //   contents of rom_2 (hex, n*v repeats v):
  //   0 62 0 63 54 54 151 0 0 6 0 0 5 5 6 0 0 62 0 8 8 54 151 0 0 6 0 0 5 5 6 0 0 62 d3 63 54 54 151 0 0 6
  //   0 0 5 5 6 0 0 62 d3 8 8 54 151 0 0 6 0 0 5 5 6 0 0 62 d4 63 54 54 151 0 0 6 0 0 5 5 6 0 0 62 d4 8 8
  //   54 151 0 0 6 0 0 5 5 6 0 0 62 0 63 54 54 151 0 0 6 0 0 5 5 6 0 0 62 0 8 8 54 151 0 0 6 0 0 5 5 6 0
  //   151 62 0 63 54 54 151 0 6 6 0 0 5 5 6 0 151 62 0 8 8 54 151 0 6 6 0 0 5 5 6 0 151 62 d3 63 54 54 151
  //   0 6 6 0 0 5 5 6 0 151 62 d3 8 8 54 151 0 6 6 0 0 5 5 6 0 151 62 d4 63 54 54 151 0 6 6 0 0 5 5 6 0
  //   151 62 d4 8 8 54 151 0 6 6 0 0 5 5 6 0 151 62 0 63 54 54 151 0 6 6 0 0 5 5 6 0 151 62 0 8 8 54 151 0
  //   6 6 0 0 5 5 6
  //   contents of rom_3 (hex, n*v repeats v):
  //   0 8f2 8d0 8f4 8e5 8c6 8c7 8c8 8c9 8ca 8cb 8cc 8cd 4ce 0 0 0 1 0 3 13*0 8f2 8d0 8f4 8e5 8c6 8c7 8c8
  //   8c9 8ca 8cb 8cc 8cd 4ce 6c0 0 0 1 0 3 13*0 8f2 8d0 8f4 8e5 8c6 8c7 8c8 8c9 8ca 8cb 8cc 8cd 4ce 5c0 0
  //   0 1 0 3 13*0 8f2 8d0 8f4 8e5 8c6 8c7 8c8 8c9 8ca 8cb 8cc 8cd 4ce 0 0 0 1 0 3 12*0 1 8f2 8d0 8f4 8e5
  //   8c6 8c7 8c8 8c9 8ca 8cb 8cc 8cd 4ce 0 0 1 1 0 3 12*0 1 8f2 8d0 8f4 8e5 8c6 8c7 8c8 8c9 8ca 8cb 8cc
  //   8cd 4ce 6c0 0 1 1 0 3 12*0 1 8f2 8d0 8f4 8e5 8c6 8c7 8c8 8c9 8ca 8cb 8cc 8cd 4ce 5c0 0 1 1 0 3 12*0
  //   1 8f2 8d0 8f4 8e5 8c6 8c7 8c8 8c9 8ca 8cb 8cc 8cd 4ce 0 0 1 1 0 3 12*0 3 8f2 8d0 8f4 8e5 8c6 8c7 8c8
  //   8c9 8ca 8cb 8cc 8cd 4ce 0 0 3 1 0 3 12*0 3 8f2 8d0 8f4 8e5 8c6 8c7 8c8 8c9 8ca 8cb 8cc 8cd 4ce 6c0 0
  //   3 1 0 3 12*0 3 8f2 8d0 8f4 8e5 8c6 8c7 8c8 8c9 8ca 8cb 8cc 8cd 4ce 5c0 0 3 1 0 3 12*0 3 8f2 8d0 8f4
  //   8e5 8c6 8c7 8c8 8c9 8ca 8cb 8cc 8cd 4ce 0 0 3 1 0 3 13*0 8f2 8d0 8f4 8e5 8c6 8c7 8c8 8c9 8ca 8cb 8cc
  //   8cd 4ce 0 0 0 1 0 3 13*0 8f2 8d0 8f4 8e5 8c6 8c7 8c8 8c9 8ca 8cb 8cc 8cd 4ce 6c0 0 0 1 0 3 13*0 8f2
  //   8d0 8f4 8e5 8c6 8c7 8c8 8c9 8ca 8cb 8cc 8cd 4ce 5c0 0 0 1 0 3 13*0 8f2 8d0 8f4 8e5 8c6 8c7 8c8 8c9
  //   8ca 8cb 8cc 8cd 4ce 0 0 0 1 0 3
  //   contents of rom_4 (hex, n*v repeats v):
  //   0 3e 38 0 0 1 0 0 1 3e 38 0 1 1
  //   contents of rom_5 (hex, n*v repeats v):
  //   0 6e 72 0 0 6e 70 0 0 1 0 0 0 1 0 0 1 6e 72 0 1 6e 70 0 1 1 0 0 1 1
  //   contents of rom_6 (hex, n*v repeats v):
  //   0 1 12 3 c 4*0 1 0 3 8 4*0 2 12 4 c 4*0 2 0 4 8 0 0 0 1 1 12 3 c 0 0 0 1 1 0 3 8 0 0 0 1 2 12 4 c 0
  //   0 0 1 2 0 4 8 0 0 0 3 1 12 3 c 0 0 0 3 1 0 3 8 0 0 0 3 2 12 4 c 0 0 0 3 2 0 4 8 4*0 1 12 3 c 4*0 1 0
  //   3 8 4*0 2 12 4 c 4*0 2 0 4 8
endmodule

module I_O (
  input  RE_WR,
  input  INT_In,
  input  [7:0] DATA_In,
  input  [7:0] Address_In,
  input  [7:0] Address,
  input  [7:0] ROM_In,
  output INT,
  output [7:0] RAM_Out,
  output ADD_Match,
  output [7:0] DATA_Out,
  output Reset_RAM,
  output Reset_ROM
);

  wire AA, AC, and_1_out, and_2_out, and_3_out, and_4_out, and_5_out, and_10_out, and_11_out, and_12_out,
       and_13_out, clock_1_out, clock_2_out, clock_3_out, clock_4_out, clock_5_out, clock_6_out, clock_7_out,
       D_55, D_77, d_ff_1_q, d_ff_1_qn, d_ff_2_q, d_ff_2_qn, d_ff_3_q, d_ff_3_qn, DATA_Out_En, EOP, INT_OFF,
       j_k_ff_2_q, not_1_out, not_2_out, not_3_out, not_4_out, not_5_out, not_6_out, not_7_out, not_8_out,
       not_9_out, not_10_out, not_11_out, not_12_out, not_13_out, not_14_out, not_15_out, not_16_out,
       not_17_out, not_18_out, not_19_out, not_21_out, not_22_out, not_23_out, not_24_out, or_1_out,
       or_4_out, WORD_SEND;
  wire [2:0] register_1_q, rom_1_data;
  wire [6:4] controlled_buffer_3_out;
  wire [7:0] controlled_buffer_1_out, DATA_Out_t;
  wire [7:7] not_20_out;

  not not_1 (not_1_out, EOP);
  and and_1 (and_1_out, d_ff_1_q, not_1_out);
  and and_2 (and_2_out, d_ff_1_q, AC);
  and and_3 (and_3_out, AC, not_1_out);
  J_K_Flip_Flop j_k_ff_1 (.J(INT_In), .K(INT_OFF), .clk(clock_1_out), .Q(INT));  // open: Qn, preset, reset
  Clock clock_1 (.out(clock_1_out));
  assign controlled_buffer_1_out = RE_WR ? RAM_Out : 8'bz;  // Controlled_Buffer controlled_buffer_1
  assign controlled_buffer_1_out = and_4_out ? DATA_Out_t : 8'bz;  // Controlled_Buffer controlled_buffer_2
  and and_4 (and_4_out, DATA_Out_En, not_2_out);
  not not_2 (not_2_out, RE_WR);
  D_Flip_Flop d_ff_1 (.D(or_1_out), .clk(clock_2_out), .Q(d_ff_1_q), .Qn(d_ff_1_qn));  // open: preset, reset
  or or_1 (or_1_out, and_1_out, and_2_out, and_3_out);
  Clock clock_2 (.out(clock_2_out));
  J_K_Flip_Flop j_k_ff_2 (.J(EOP), .K(INT), .clk(clock_3_out), .Q(j_k_ff_2_q));  // open: Qn, preset, reset
  Clock clock_3 (.out(clock_3_out));
  not not_3 (not_3_out, controlled_buffer_1_out[1]);
  not not_4 (not_4_out, controlled_buffer_1_out[3]);
  not not_5 (not_5_out, controlled_buffer_1_out[5]);
  not not_6 (not_6_out, controlled_buffer_1_out[7]);
  not not_7 (not_7_out, controlled_buffer_1_out[0]);
  not not_8 (not_8_out, controlled_buffer_1_out[2]);
  not not_9 (not_9_out, controlled_buffer_1_out[4]);
  not not_10 (not_10_out, controlled_buffer_1_out[6]);
  and and_5 (and_5_out, d_ff_1_qn, not_1_out, AC);
  and and_6 (D_55, controlled_buffer_1_out[0], not_3_out, controlled_buffer_1_out[2], not_4_out, controlled_buffer_1_out[4], not_5_out, controlled_buffer_1_out[6], not_6_out);
  and and_7 (AA, not_7_out, controlled_buffer_1_out[1], not_8_out, controlled_buffer_1_out[3], not_9_out, controlled_buffer_1_out[5], not_10_out, controlled_buffer_1_out[7]);
  or or_2 (Reset_RAM, and_5_out, INT, EOP);
  or or_3 (Reset_ROM, AC, INT, j_k_ff_2_q);
  Register #(.width(3)) register_1 (.D(rom_1_data), .en(1'b1), .clk(clock_4_out), .Q(register_1_q));  // open: clr
  Clock clock_4 (.out(clock_4_out));
  assign controlled_buffer_3_out[4] = ADD_Match ? AC : 1'bz;  // Controlled_Buffer controlled_buffer_3
  assign controlled_buffer_3_out[4] = not_11_out ? 1'b0 : 1'bz;  // Controlled_Buffer controlled_buffer_4
  assign controlled_buffer_3_out[6] = ADD_Match ? D_77 : 1'bz;  // Controlled_Buffer controlled_buffer_5
  assign controlled_buffer_3_out[6] = not_11_out ? 1'b0 : 1'bz;  // Controlled_Buffer controlled_buffer_6
  not not_11 (not_11_out, ADD_Match);
  Comparator comparator_1 (.a(Address_In), .b(Address), .eq(ADD_Match));  // open: gt, lt
  assign DATA_Out = DATA_Out_En ? DATA_Out_t : 8'bz;  // Controlled_Buffer controlled_buffer_7
  ROM #(.dataWidth(6)) rom_1 (
    .addr({ADD_Match, controlled_buffer_3_out[6], RE_WR, controlled_buffer_3_out[4], EOP, register_1_q}),
    .data({DATA_Out_En, INT_OFF, WORD_SEND, rom_1_data}));
  assign RAM_Out = ADD_Match ? DATA_In : 8'bz;  // Controlled_Buffer controlled_buffer_8
  not not_12 (not_12_out, ADD_Match);
  assign DATA_Out_t = not_13_out ? ROM_In : 8'bz;  // Controlled_Buffer controlled_buffer_9
  not not_13 (not_13_out, WORD_SEND);
  assign RAM_Out = not_12_out ? {8{1'b0}} : 8'bz;  // Controlled_Buffer controlled_buffer_10
  assign DATA_Out_t = WORD_SEND ? {not_20_out[7], {2{RE_WR}}, {2{not_20_out[7]}}, {2{RE_WR}}, not_20_out[7]} : 8'bz;  // Controlled_Buffer controlled_buffer_11
  not not_14 (not_14_out, RAM_Out[3]);
  not not_15 (not_15_out, RAM_Out[7]);
  not not_16 (not_16_out, RAM_Out[0]);
  not not_17 (not_17_out, RAM_Out[1]);
  not not_18 (not_18_out, RAM_Out[4]);
  not not_19 (not_19_out, RAM_Out[6]);
  not not_20 (not_20_out[7], RE_WR);
  and and_8 (D_77, RAM_Out[0], RAM_Out[1], RAM_Out[2], not_14_out, RAM_Out[4], RAM_Out[5], RAM_Out[6], not_15_out);
  and and_9 (AC, not_16_out, not_17_out, RAM_Out[2], RAM_Out[3], not_18_out, RAM_Out[5], not_19_out, RAM_Out[7]);
  not not_21 (not_21_out, D_55);
  or or_4 (or_4_out, and_11_out, and_10_out);
  and and_10 (and_10_out, D_55, not_23_out, d_ff_2_q, d_ff_3_qn);
  and and_11 (and_11_out, d_ff_3_q, d_ff_2_qn, not_22_out, AA);
  not not_22 (not_22_out, D_55);
  not not_23 (not_23_out, AA);
  D_Flip_Flop d_ff_2 (.D(and_12_out), .clk(clock_5_out), .Q(d_ff_2_q), .Qn(d_ff_2_qn));  // open: preset, reset
  and and_12 (and_12_out, d_ff_2_qn, AA, not_21_out);
  Clock clock_5 (.out(clock_5_out));
  D_Flip_Flop d_ff_3 (.D(or_4_out), .clk(clock_6_out), .Q(d_ff_3_q), .Qn(d_ff_3_qn));  // open: preset, reset
  Clock clock_6 (.out(clock_6_out));
  not not_24 (not_24_out, AA);
  D_Flip_Flop d_ff_4 (.D(and_13_out), .clk(clock_7_out), .Q(EOP));  // open: Qn, preset, reset
  and and_13 (and_13_out, d_ff_2_q, d_ff_3_q, D_55, not_24_out);
  Clock clock_7 (.out(clock_7_out));

  // Other names for the same wires on the sheet: ADD = ADD_Match; DATA_In_t[7:0] = RAM_Out

  // Notes on the sheet:
  //   READ=1
  //   WRITE=0
  //   55
  //   AA
  //   contents of rom_1 (hex, n*v repeats v):
  //   0 2a 2 24 24 4*0 2a 2 6*0 2a 2 24 24 4*0 2a 2 6*0 2a 2 0 0 5 0 0 0 2a 2 0 5 4*0 2a 2 0 0 5 0 0 0 2a
  //   2 0 5 4*0 2a 2 24 24 4*0 2a 2 6*0 2a 2 24 24 4*0 2a 2 6*0 2a 2 0 0 5 0 0 0 2a 2 0 5 4*0 2a 2 0 0 5 0
  //   0 0 2a 2 0 5 4*0 1 0 3 3 4*0 1 0 3 3 4*0 1 3 3 3 4*0 1 3 3 3 4*0 1 0 5 3 5 0 0 0 1 0 0 3 4*0 1 3 5 3
  //   5 0 0 0 1 3 0 3 0 0 0 11 1 0 3 3 0 0 0 11 1 0 3 3 0 0 0 11 1 3 3 3 0 0 0 11 1 3 3 3 0 0 0 11 1 0 5 3
  //   5 0 0 11 1 0 0 3 0 0 0 11 1 3 5 3 5 0 0 11 1 3 0 3
  //   77
  //   AC
endmodule
